# Fritzing sketch balloonlogger breadboard (saved by Fritzing 0.9.3b)
circuit board: 8.46667cm x 5.64444cm
breadboards: 2

parts:
  Raspberry_Pi_Zero1 = Raspberry Pi Zero
  DS1 = DS18B20 1-Wire Temperature Sensor [part_number=DS18B20]
  Part1 = Adafruit_BMP280
  R1 = Resistor [tolerance=±5% resistance=4.7k package=THT]
  J1 = Camdenboss CTB0158-3 [part_number=CTB0158-3 package=THT]
  S1 = Momentary Switch [package=ksa_sealed_tac_switch]
  Part3 = Adafruit_BMP280
  J2 = Camdenboss CTB0158-3 [part_number=CTB0158-3 package=THT]
  S2 = Momentary Switch [package=ksa_sealed_tac_switch]
  R8 = Resistor [tolerance=±5% resistance=4.7k package=THT]
  LED10 = RGB LED (com. cathode, rbg) [package="5 mm [THT]"]
  R9 = Resistor [tolerance=±5% resistance=100 package=THT]
  R10 = Resistor [tolerance=±5% resistance=1k package=THT]
  R11 = Resistor [tolerance=±5% resistance=1k package=THT]

nets:
  3V3: Raspberry_Pi_Zero1.3v3, Raspberry_Pi_Zero1.3V3, R1.Pin_0, J1.pin2
  N1: Raspberry_Pi_Zero1.GPIO2, Part1.SDI/SDA
  N2: Raspberry_Pi_Zero1.GPIO3, Part1.SCK/SCL
  N3: Raspberry_Pi_Zero1.GPIO4, R1.Pin_1, J1.pin1
  GND: Raspberry_Pi_Zero1.GND, Part1.GND, J1.pin3, S1.2, LED10.common_cathode
  N4: Raspberry_Pi_Zero1.GPIO17, R9.Pin_1
  N5: Raspberry_Pi_Zero1.GPIO27, R10.Pin_1
  N6: Raspberry_Pi_Zero1.GPIO22, R11.Pin_1
  N7: Raspberry_Pi_Zero1.GPIO23, S1.4
  5V: Raspberry_Pi_Zero1.5V, Part1.VIN
  N8: DS1.GND, J1.terminal_3
  N9: DS1.DQ, J1.terminal_1
  N10: DS1.VDD, J1.terminal_2
  N11: Part3.GND, J2.pin3, S2.3
  N12: J2.pin1, R8.Pin_1
  N13: J2.pin2, R8.Pin_0
  N14: LED10.red_anode, R9.Pin_0
  N15: LED10.blue_anode, R10.Pin_0
  N16: LED10.green_anode, R11.Pin_0

custom parts:
  Adafruit_BMP280: Bosch has stepped up their game with their new BMP280 sensor, an environmental sensor with temperature, barometric pressure that is the next generation upgrade to the BMP085/BMP180/BMP183. This sensor is great for all sorts of weather sensing and can even be used in both I2C and SPI! This precision sensor from Bosch is the best low-cost, precision sensing solution for measuring barometric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
